// Logisim project BancoRegistradores32Bits.circ as structural Verilog: 1 circuit, main circuit BancoRegistradores
module BancoRegistradores (
  input  [31:0] WD,
  input  in_2,
  input  [4:0] LR1,
  input  [4:0] LR2,
  input  RegWrite,
  input  [4:0] WR,
  output [31:0] LD1,
  output [31:0] LD2
);

  wire clock_1_out, demultiplexer_1_out1, demultiplexer_1_out2, demultiplexer_1_out3, demultiplexer_1_out4,
       demultiplexer_1_out5, demultiplexer_1_out6, demultiplexer_1_out7, demultiplexer_1_out8,
       demultiplexer_1_out9, demultiplexer_1_out10, demultiplexer_1_out11, demultiplexer_1_out12,
       demultiplexer_1_out13, demultiplexer_1_out14, demultiplexer_1_out15, demultiplexer_1_out16,
       demultiplexer_1_out17, demultiplexer_1_out18, demultiplexer_1_out19, demultiplexer_1_out20,
       demultiplexer_1_out21, demultiplexer_1_out22, demultiplexer_1_out23, demultiplexer_1_out24,
       demultiplexer_1_out25, demultiplexer_1_out26, demultiplexer_1_out27, demultiplexer_1_out28,
       demultiplexer_1_out29, demultiplexer_1_out30, demultiplexer_1_out31;
  wire [31:0] S0, S1, S2, S3, S4, S5, S6, S7, S8, S9, S10, S11, S12, S13, S14, S15, S16, S17, S18, S19, S20,
       S21, S22, S23, S24, S25, S26, S27, S28, S29, S30, S31;

  Clock clock_1 (.out(clock_1_out));
  Demultiplexer #(.select(5)) demultiplexer_1 (
    .out1(demultiplexer_1_out1), .out2(demultiplexer_1_out2), .out3(demultiplexer_1_out3),
    .out4(demultiplexer_1_out4), .out5(demultiplexer_1_out5), .out6(demultiplexer_1_out6),
    .out7(demultiplexer_1_out7), .out8(demultiplexer_1_out8), .out9(demultiplexer_1_out9),
    .out10(demultiplexer_1_out10), .out11(demultiplexer_1_out11), .out12(demultiplexer_1_out12),
    .out13(demultiplexer_1_out13), .out14(demultiplexer_1_out14), .out15(demultiplexer_1_out15),
    .out16(demultiplexer_1_out16), .out17(demultiplexer_1_out17), .out18(demultiplexer_1_out18),
    .out19(demultiplexer_1_out19), .out20(demultiplexer_1_out20), .out21(demultiplexer_1_out21),
    .out22(demultiplexer_1_out22), .out23(demultiplexer_1_out23), .out24(demultiplexer_1_out24),
    .out25(demultiplexer_1_out25), .out26(demultiplexer_1_out26), .out27(demultiplexer_1_out27),
    .out28(demultiplexer_1_out28), .out29(demultiplexer_1_out29), .out30(demultiplexer_1_out30),
    .out31(demultiplexer_1_out31), .in(RegWrite), .sel(WR));  // open: out0
  Register #(.width(32)) register_1 (.D(WD), .en(in_2), .clk(clock_1_out), .Q(S0));  // open: clr
  Register #(.width(32)) register_2 (.D(WD), .en(demultiplexer_1_out1), .clk(clock_1_out), .Q(S1));  // open: clr
  Register #(.width(32)) register_3 (.D(WD), .en(demultiplexer_1_out2), .clk(clock_1_out), .Q(S2));  // open: clr
  Register #(.width(32)) register_4 (.D(WD), .en(demultiplexer_1_out3), .clk(clock_1_out), .Q(S3));  // open: clr
  Register #(.width(32)) register_5 (.D(WD), .en(demultiplexer_1_out4), .clk(clock_1_out), .Q(S4));  // open: clr
  Register #(.width(32)) register_6 (.D(WD), .en(demultiplexer_1_out5), .clk(clock_1_out), .Q(S5));  // open: clr
  Register #(.width(32)) register_7 (.D(WD), .en(demultiplexer_1_out6), .clk(clock_1_out), .Q(S6));  // open: clr
  Register #(.width(32)) register_8 (.D(WD), .en(demultiplexer_1_out7), .clk(clock_1_out), .Q(S7));  // open: clr
  Register #(.width(32)) register_9 (.D(WD), .en(demultiplexer_1_out8), .clk(clock_1_out), .Q(S8));  // open: clr
  Register #(.width(32)) register_10 (.D(WD), .en(demultiplexer_1_out9), .clk(clock_1_out), .Q(S9));  // open: clr
  Register #(.width(32)) register_11 (.D(WD), .en(demultiplexer_1_out10), .clk(clock_1_out), .Q(S10));  // open: clr
  Register #(.width(32)) register_12 (.D(WD), .en(demultiplexer_1_out11), .clk(clock_1_out), .Q(S11));  // open: clr
  Register #(.width(32)) register_13 (.D(WD), .en(demultiplexer_1_out12), .clk(clock_1_out), .Q(S12));  // open: clr
  Register #(.width(32)) register_14 (.D(WD), .en(demultiplexer_1_out13), .clk(clock_1_out), .Q(S13));  // open: clr
  Register #(.width(32)) register_15 (.D(WD), .en(demultiplexer_1_out14), .clk(clock_1_out), .Q(S14));  // open: clr
  Register #(.width(32)) register_16 (.D(WD), .en(demultiplexer_1_out15), .clk(clock_1_out), .Q(S15));  // open: clr
  Register #(.width(32)) register_17 (.D(WD), .en(demultiplexer_1_out16), .clk(clock_1_out), .Q(S16));  // open: clr
  Register #(.width(32)) register_18 (.D(WD), .en(demultiplexer_1_out17), .clk(clock_1_out), .Q(S17));  // open: clr
  Register #(.width(32)) register_19 (.D(WD), .en(demultiplexer_1_out18), .clk(clock_1_out), .Q(S18));  // open: clr
  Register #(.width(32)) register_20 (.D(WD), .en(demultiplexer_1_out19), .clk(clock_1_out), .Q(S19));  // open: clr
  Register #(.width(32)) register_21 (.D(WD), .en(demultiplexer_1_out20), .clk(clock_1_out), .Q(S20));  // open: clr
  Register #(.width(32)) register_22 (.D(WD), .en(demultiplexer_1_out21), .clk(clock_1_out), .Q(S21));  // open: clr
  Register #(.width(32)) register_23 (.D(WD), .en(demultiplexer_1_out22), .clk(clock_1_out), .Q(S22));  // open: clr
  Register #(.width(32)) register_24 (.D(WD), .en(demultiplexer_1_out23), .clk(clock_1_out), .Q(S23));  // open: clr
  Register #(.width(32)) register_25 (.D(WD), .en(demultiplexer_1_out24), .clk(clock_1_out), .Q(S24));  // open: clr
  Register #(.width(32)) register_26 (.D(WD), .en(demultiplexer_1_out25), .clk(clock_1_out), .Q(S25));  // open: clr
  Register #(.width(32)) register_27 (.D(WD), .en(demultiplexer_1_out26), .clk(clock_1_out), .Q(S26));  // open: clr
  Register #(.width(32)) register_28 (.D(WD), .en(demultiplexer_1_out27), .clk(clock_1_out), .Q(S27));  // open: clr
  Register #(.width(32)) register_29 (.D(WD), .en(demultiplexer_1_out28), .clk(clock_1_out), .Q(S28));  // open: clr
  Register #(.width(32)) register_30 (.D(WD), .en(demultiplexer_1_out29), .clk(clock_1_out), .Q(S29));  // open: clr
  Register #(.width(32)) register_31 (.D(WD), .en(demultiplexer_1_out30), .clk(clock_1_out), .Q(S30));  // open: clr
  Register #(.width(32)) register_32 (.D(WD), .en(demultiplexer_1_out31), .clk(clock_1_out), .Q(S31));  // open: clr
  Multiplexer #(.select(5), .width(32)) multiplexer_1 (
    .in0(S0), .in1(S1), .in2(S2), .in3(S3), .in4(S4), .in5(S5), .in6(S6), .in7(S7), .in8(S8), .in9(S9),
    .in10(S10), .in11(S11), .in12(S12), .in13(S13), .in14(S14), .in15(S15), .in16(S16), .in17(S17),
    .in18(S18), .in19(S19), .in20(S20), .in21(S21), .in22(S22), .in23(S23), .in24(S24), .in25(S25),
    .in26(S26), .in27(S27), .in28(S28), .in29(S29), .in30(S30), .in31(S31), .out(LD1), .sel(LR1));
  Multiplexer #(.select(5), .width(32)) multiplexer_2 (
    .in0(S0), .in1(S1), .in2(S2), .in3(S3), .in4(S4), .in5(S5), .in6(S6), .in7(S7), .in8(S8), .in9(S9),
    .in10(S10), .in11(S11), .in12(S12), .in13(S13), .in14(S14), .in15(S15), .in16(S16), .in17(S17),
    .in18(S18), .in19(S19), .in20(S20), .in21(S21), .in22(S22), .in23(S23), .in24(S24), .in25(S25),
    .in26(S26), .in27(S27), .in28(S28), .in29(S29), .in30(S30), .in31(S31), .out(LD2), .sel(LR2));
endmodule
