// Logisim project Decodificador.circ as structural Verilog: 1 circuit, main circuit Decodificador
module Decodificador (
  input  [31:0] Instrucao,
  output [25:0] Addr,
  output [15:0] Imm,
  output [5:0] funct,
  output [4:0] shmt,
  output [4:0] rd,
  output [4:0] rt,
  output [4:0] rs,
  output [5:0] Opcode
);


  assign Addr = Instrucao[25:0];
  assign funct = Instrucao[5:0];
  assign Imm = Instrucao[15:0];
  assign Opcode = Instrucao[31:26];
  assign rd = Instrucao[15:11];
  assign rs = Instrucao[25:21];
  assign rt = Instrucao[20:16];
  assign shmt = Instrucao[10:6];
endmodule
