// Logisim project ULA.circ as structural Verilog: 5 circuits, main circuit ULA
module ULA (
  input  [31:0] A,
  input  [31:0] B,
  input  [4:0] SHMT,
  input  [2:0] opALU,
  output Overflow,
  output [31:0] Resultado,
  output Zero
);

  wire comparator_1_lt, pegar_msb_1_out_2, pegar_msb_2_out_2, pegar_msb_3_out_2;
  wire [31:0] adder_1_out, adder_2_out, and_1_out, conversao1bit_1_out_2, or_1_out, shifter_1_out,
       shifter_2_out, subtractor_1_out;

  Adder #(.width(32)) adder_1 (.a(A), .b(B), .out(adder_1_out));  // open: cin, cout
  Shifter #(.width(32)) shifter_1 (.in(A), .\dist (SHMT), .out(shifter_1_out));
  Shifter #(.shift("lr"), .width(32)) shifter_2 (.in(A), .\dist (SHMT), .out(shifter_2_out));
  Comparator #(.width(32)) comparator_1 (.a(A), .b(A), .lt(comparator_1_lt));  // open: gt, eq
  assign or_1_out = A | B;  // OR_Gate or_1, 32 bits wide
  assign and_1_out = A & B;  // AND_Gate and_1, 32 bits wide
  Adder #(.width(32)) adder_2 (.a(A), .b(B), .out(adder_2_out));  // open: cin, cout
  Subtractor #(.width(32)) subtractor_1 (.a(A), .b(B), .out(subtractor_1_out));  // open: bin, bout
  conversao1bit conversao1bit_1 (.in_1(comparator_1_lt), .out_2(conversao1bit_1_out_2));
  Multiplexer #(.select(3), .width(32)) multiplexer_1 (
    .in0(adder_1_out), .in1(shifter_1_out), .in2(shifter_2_out), .in3(conversao1bit_1_out_2), .in4(or_1_out),
    .in5(and_1_out), .in6(adder_2_out), .in7(subtractor_1_out), .out(Resultado), .sel(opALU));
  Pegar_MSB pegar_msb_1 (.in_1(A), .out_2(pegar_msb_1_out_2));
  Pegar_MSB pegar_msb_2 (.in_1(B), .out_2(pegar_msb_2_out_2));
  Pegar_MSB pegar_msb_3 (.in_1(Resultado), .out_2(pegar_msb_3_out_2));
  overflowsomasub overflowsomasub_1 (
    .OPCODE(opALU), .A(pegar_msb_1_out_2), .B(pegar_msb_2_out_2), .Resultado(pegar_msb_3_out_2),
    .overflow(Overflow));
  ehZero ehzero_1 (.in_1(Resultado), .out_2(Zero));

  // Notes on the sheet:
  //   1 to 32
  //   000 - ADDU
  //   001 - SLL
  //   010 - SRL
  //   011 - SLT
  //   100 - OR
  //   101 - AND
  //   110 - ADD
  //   111 - SUB
endmodule

module ehZero (
  input  [31:0] in_1,
  output out_2
);

  and and_1 (out_2, ~in_1[0], ~in_1[1], ~in_1[2], ~in_1[3], ~in_1[4], ~in_1[5], ~in_1[6], ~in_1[7], ~in_1[8], ~in_1[9], ~in_1[10], ~in_1[11], ~in_1[12], ~in_1[13], ~in_1[14], ~in_1[15], ~in_1[16], ~in_1[17], ~in_1[18], ~in_1[19], ~in_1[20], ~in_1[21], ~in_1[22], ~in_1[23], ~in_1[24], ~in_1[25], ~in_1[26], ~in_1[27], ~in_1[28], ~in_1[29], ~in_1[30], ~in_1[31]);  // AND_Gate
endmodule

module conversao1bit (
  input  in_1,
  output [31:0] out_2
);

  not not_1 (out_2[31], 1'b1);

  assign out_2[30:0] = {{30{out_2[31]}}, in_1};
endmodule

module Pegar_MSB (
  input  [31:0] in_1,
  output out_2
);


  assign out_2 = in_1[31];
endmodule

module overflowsomasub (
  input  [2:0] OPCODE,
  input  A,
  input  B,
  input  Resultado,
  output overflow
);

  wire and_1_out, and_2_out, and_3_out, and_4_out, and_5_out, and_6_out;

  and and_1 (and_1_out, OPCODE[2], OPCODE[1], ~OPCODE[0]);  // AND_Gate
  and and_2 (and_2_out, OPCODE[2], OPCODE[1], OPCODE[0]);
  and and_3 (and_3_out, and_1_out, A, B, ~Resultado);  // AND_Gate
  and and_4 (and_4_out, and_1_out, ~A, ~B, Resultado);  // AND_Gate
  and and_5 (and_5_out, and_2_out, ~A, B, Resultado);  // AND_Gate
  and and_6 (and_6_out, and_2_out, A, ~B, ~Resultado);  // AND_Gate
  or or_1 (overflow, and_3_out, and_4_out, and_5_out, and_6_out);

  // Notes on the sheet:
  //   add
  //   sub
endmodule
