// Logisim project extensor16para32bits.circ as structural Verilog: 1 circuit, main circuit extensor16para32bits
module extensor16para32bits (
  input  [15:0] imm16bits,
  output [31:0] imm32bits
);


  assign imm32bits = {{17{imm16bits[15]}}, imm16bits[14:0]};
endmodule
