// Logisim project unidadeControle.circ as structural Verilog: 1 circuit, main circuit UnidadeControle
module UnidadeControle (
  input  [5:0] Opcode,
  output [2:0] AluOP,
  output Jump,
  output RegDst,
  output Regwrite,
  output AluSRC,
  output MemToReg,
  output MemRead,
  output MemWrite,
  output BRENCH
);

  wire ADDI_out, ANDI_out, ORI_out, SLTI_out;

  and R (RegDst, ~Opcode[0], ~Opcode[1], ~Opcode[2], ~Opcode[3], ~Opcode[4], ~Opcode[5]);  // AND_Gate
  and ADDI (ADDI_out, Opcode[0], Opcode[1], Opcode[2], ~Opcode[3], Opcode[4], Opcode[5]);  // AND_Gate
  and ANDI (ANDI_out, ~Opcode[0], ~Opcode[1], Opcode[2], Opcode[3], ~Opcode[4], ~Opcode[5]);  // AND_Gate
  and ORI (ORI_out, Opcode[0], ~Opcode[1], Opcode[2], Opcode[3], ~Opcode[4], ~Opcode[5]);  // AND_Gate
  and SLTI (SLTI_out, ~Opcode[0], Opcode[1], ~Opcode[2], Opcode[3], ~Opcode[4], ~Opcode[5]);  // AND_Gate
  and LW (MemRead, Opcode[0], Opcode[1], ~Opcode[2], ~Opcode[3], Opcode[4], ~Opcode[5]);  // AND_Gate
  and SW (MemWrite, Opcode[0], Opcode[1], ~Opcode[2], Opcode[3], ~Opcode[4], Opcode[5]);  // AND_Gate
  and BEQ (BRENCH, ~Opcode[0], ~Opcode[1], Opcode[2], ~Opcode[3], ~Opcode[4], ~Opcode[5]);  // AND_Gate
  and J (Jump, ~Opcode[0], Opcode[1], ~Opcode[2], ~Opcode[3], ~Opcode[4], ~Opcode[5]);  // AND_Gate
  or or_1 (Regwrite, RegDst, ADDI_out, ANDI_out, ORI_out, SLTI_out, MemRead);
  or or_2 (AluSRC, ADDI_out, ANDI_out, ORI_out, SLTI_out, MemRead, MemWrite);
  or or_3 (AluOP[2], ADDI_out, ANDI_out, ORI_out, MemRead, MemWrite, BRENCH);
  or or_4 (AluOP[1], ADDI_out, SLTI_out, MemRead, MemWrite, BRENCH);
  or or_5 (AluOP[0], SLTI_out, BRENCH);

  assign MemToReg = MemRead;
endmodule
