// Logisim project unidadeControleULA.circ as structural Verilog: 4 circuits, main circuit unidadecontroleULA
module unidadecontroleULA (
  input  [5:0] Funct,
  input  [2:0] AluOP,
  output [2:0] OpULA
);

  wire ehtudozero_1_out_2, not_1_out;
  wire [2:0] bits6para3_1_out_2;
  wire [5:0] functvirarinstrucao_1_out_2;

  FunctVirarInstrucao functvirarinstrucao_1 (.in_1(Funct), .out_2(functvirarinstrucao_1_out_2));
  bits6para3 bits6para3_1 (.in_1(functvirarinstrucao_1_out_2), .out_2(bits6para3_1_out_2));
  Multiplexer #(.width(3)) multiplexer_1 (.in0(bits6para3_1_out_2), .in1(AluOP), .out(OpULA), .sel(not_1_out));
  not not_1 (not_1_out, ehtudozero_1_out_2);
  ehtudoZERO ehtudozero_1 (.in_1(AluOP), .out_2(ehtudozero_1_out_2));
endmodule

module bits6para3 (
  input  [5:0] in_1,
  output [2:0] out_2
);


  assign out_2 = in_1[2:0];
endmodule

module ehtudoZERO (
  input  [2:0] in_1,
  output out_2
);

  and and_1 (out_2, ~in_1[0], ~in_1[1], ~in_1[2]);  // AND_Gate
endmodule

module FunctVirarInstrucao (
  input  [5:0] in_1,
  output [5:0] out_2
);

  wire ADD_out, addu_out, AMD_out, ORR_out, SLLL_out, SLTT_out, SRLL_out, sub_out;

  and ADD (ADD_out, ~in_1[0], ~in_1[1], ~in_1[2], ~in_1[3], ~in_1[4], in_1[5]);  // AND_Gate
  or addu (addu_out, in_1[0], ~in_1[1], ~in_1[2], ~in_1[3], ~in_1[4], in_1[5]);  // OR_Gate
  and sub (sub_out, in_1[0], ~in_1[1], ~in_1[2], ~in_1[3], in_1[4], ~in_1[5]);  // AND_Gate
  and AMD (AMD_out, in_1[0], ~in_1[1], ~in_1[2], in_1[3], ~in_1[4], ~in_1[5]);  // AND_Gate
  and ORR (ORR_out, in_1[0], ~in_1[1], ~in_1[2], in_1[3], ~in_1[4], in_1[5]);  // AND_Gate
  and SLLL (SLLL_out, ~in_1[0], ~in_1[1], ~in_1[2], ~in_1[3], ~in_1[4], ~in_1[5]);  // AND_Gate
  and SRLL (SRLL_out, ~in_1[0], ~in_1[1], ~in_1[2], in_1[3], ~in_1[4], in_1[5]);  // AND_Gate
  and SLTT (SLTT_out, in_1[0], ~in_1[1], in_1[2], ~in_1[3], in_1[4], ~in_1[5]);  // AND_Gate
  or or_1 (out_2[5], ADD_out, sub_out, AMD_out, ORR_out);
  or or_2 (out_2[1], ADD_out, sub_out, SRLL_out, SLTT_out);
  or or_3 (out_2[0], sub_out, AMD_out, SLLL_out, SLTT_out);

  assign out_2[4:2] = {3{out_2[5]}};
endmodule
