// Logisim project CaminhoDeDados.circ as structural Verilog: 17 circuits, main circuit caminhoDados
module caminhoDados (
  output [5:0] opcode,
  output [4:0] rs,
  output [4:0] rt,
  output [4:0] rd,
  output [4:0] shmt,
  output [5:0] funct,
  output [15:0] imm16,
  output [25:0] addr26,
  output [31:0] PCatualMais4,
  output [31:0] addr32,
  output [31:0] resultado,
  output [31:0] a,
  output [31:0] b,
  output Zero,
  output overflow,
  output [31:0] PCrecebendo
);

  wire aluSRC, and_1_out, and_2_out, beqq, BNE, clk, Jump, MemRead, MemToReg, MemWrite, or_1_out, RegDST,
       RegWrite;
  wire [2:0] AluOP, unidadecontroleula_1_opalu;
  wire [4:0] multiplexer_3_out;
  wire [31:0] adder_1_out, bancoregistradores_1_ld2, imm32, memdados_1_dadoslidos, meminstr_1_instrucao,
       multiplexer_1_out, multiplexer_5_out, PC_q, shifter_1_out;

  Clock clock_1 (.out(clk));
  Shifter #(.width(32)) shifter_1 (.in(imm32), .\dist (5'b00010), .out(shifter_1_out));
  Adder #(.width(32)) adder_1 (.a(PCatualMais4), .b(shifter_1_out), .out(adder_1_out));  // open: cin, cout
  and and_1 (and_1_out, ~Zero, BNE);  // AND_Gate
  Multiplexer #(.width(32)) multiplexer_1 (
    .in0(PCatualMais4), .in1(adder_1_out), .out(multiplexer_1_out), .sel(or_1_out));
  or or_1 (or_1_out, and_1_out, and_2_out);
  and and_2 (and_2_out, Zero, beqq);
  transformarADDR transformaraddr_1 (.addr26(addr26), .PCatual(PCatualMais4), .addr32(addr32));
  Multiplexer #(.width(32)) multiplexer_2 (.in0(multiplexer_1_out), .in1(addr32), .out(PCrecebendo), .sel(Jump));
  Register #(.width(32)) PC (.D(PCrecebendo), .en(1'b1), .clk(clk), .Q(PC_q));  // open: clr
  Adder #(.width(32)) adder_2 (.a(32'h4), .b(PC_q), .out(PCatualMais4));  // open: cin, cout
  meminstr meminstr_1 (.PcAdress(PC_q), .Instrucao(meminstr_1_instrucao));
  Decodificador decodificador_1 (
    .Instrucao(meminstr_1_instrucao), .Addr(addr26), .Imm(imm16), .funct(funct), .shmt(shmt), .rd(rd),
    .rt(rt), .rs(rs), .Opcode(opcode));
  Multiplexer #(.width(5)) multiplexer_3 (.in0(rt), .in1(rd), .out(multiplexer_3_out), .sel(RegDST));
  UnidadeControle unidadecontrole_1 (
    .Opcode(opcode), .bitsUCselecionados(AluOP), .Jump(Jump), .RegDst(RegDST), .Regwrite(RegWrite),
    .AluSRC(aluSRC), .MemToReg(MemToReg), .MemRead(MemRead), .MemWrite(MemWrite), .beqq(beqq), .BNEEE(BNE));
  BancoRegistradores bancoregistradores_1 (
    .WD(multiplexer_5_out), .clock(clk), .LR1(rs), .LR2(rt), .RegWrite(RegWrite), .WR(multiplexer_3_out),
    .LD1(a), .LD2(bancoregistradores_1_ld2));
  extensor16para32bits extensor16para32bits_1 (.imm16bits(imm16), .imm32bits(imm32));
  unidadecontroleULA unidadecontroleula_1 (
    .Funct(funct), .bitsUCselecionados(AluOP), .OpALU(unidadecontroleula_1_opalu));
  Multiplexer #(.width(32)) multiplexer_4 (.in0(bancoregistradores_1_ld2), .in1(imm32), .out(b), .sel(aluSRC));
  ULA ula_1 (
    .A(a), .B(b), .SHMT(shmt), .opALU(unidadecontroleula_1_opalu), .Overflow(overflow),
    .ResultadoULA(resultado), .Zero(Zero));
  memdados memdados_1 (
    .endereco(resultado), .escreveDado(bancoregistradores_1_ld2), .clk(clk), .MemWrite(MemWrite),
    .MemRead(MemRead), .dadosLidos(memdados_1_dadoslidos));
  Multiplexer #(.width(32)) multiplexer_5 (
    .in0(resultado), .in1(memdados_1_dadoslidos), .out(multiplexer_5_out), .sel(MemToReg));

  // Other names for the same wires on the sheet: PCrecebe[31:0] = PCrecebendo
endmodule

module unidadecontroleULA (
  input  [5:0] Funct,
  input  [2:0] bitsUCselecionados,
  output [2:0] OpALU
);

  wire ehtudozero_1_ehtipor, not_1_out;
  wire [2:0] bits6para3_1_out_2;
  wire [5:0] functvirarinstrucao_1_out_2;

  FunctVirarInstrucao functvirarinstrucao_1 (.Funct(Funct), .out_2(functvirarinstrucao_1_out_2));
  bits6para3 bits6para3_1 (.in_1(functvirarinstrucao_1_out_2), .out_2(bits6para3_1_out_2));
  Multiplexer #(.width(3)) multiplexer_1 (
    .in0(bits6para3_1_out_2), .in1(bitsUCselecionados), .out(OpALU), .sel(not_1_out));
  not not_1 (not_1_out, ehtudozero_1_ehtipor);
  ehtudoZERO ehtudozero_1 (.bitsUCselecionados(bitsUCselecionados), .EHTipoR(ehtudozero_1_ehtipor));
endmodule

module bits6para3 (
  input  [5:0] in_1,
  output [2:0] out_2
);


  assign out_2 = in_1[2:0];
endmodule

module ehtudoZERO (
  input  [2:0] bitsUCselecionados,
  output EHTipoR
);

  and and_1 (EHTipoR, ~bitsUCselecionados[0], ~bitsUCselecionados[1], ~bitsUCselecionados[2]);  // AND_Gate
endmodule

module FunctVirarInstrucao (
  input  [5:0] Funct,
  output [5:0] out_2
);

  wire ADD_out, AMD_out, ORR_out, SLLL_out, SLTT_out, SRLL_out, sub_out;

  and ADD (ADD_out, ~Funct[0], ~Funct[1], ~Funct[2], ~Funct[3], ~Funct[4], Funct[5]);  // AND_Gate
  // AND_Gate xorr has open pins: in0=Funct[0], in1=Funct[1], in2=Funct[2], in3=Funct[3], in4=Funct[4], in5=Funct[5], out=open
  and sub (sub_out, ~Funct[0], Funct[1], ~Funct[2], ~Funct[3], ~Funct[4], Funct[5]);  // AND_Gate
  and AMD (AMD_out, ~Funct[0], ~Funct[1], Funct[2], ~Funct[3], ~Funct[4], Funct[5]);  // AND_Gate
  and ORR (ORR_out, Funct[0], ~Funct[1], Funct[2], ~Funct[3], ~Funct[4], Funct[5]);  // AND_Gate
  and SLLL (SLLL_out, ~Funct[0], ~Funct[1], ~Funct[2], ~Funct[3], ~Funct[4], ~Funct[5]);  // AND_Gate
  and SRLL (SRLL_out, ~Funct[0], Funct[1], ~Funct[2], ~Funct[3], ~Funct[4], ~Funct[5]);  // AND_Gate
  and SLTT (SLTT_out, ~Funct[0], Funct[1], ~Funct[2], Funct[3], ~Funct[4], Funct[5]);  // AND_Gate
  or or_1 (out_2[5], ADD_out, sub_out, AMD_out, ORR_out);
  or or_2 (out_2[1], ADD_out, sub_out, SRLL_out, SLTT_out);
  or or_3 (out_2[0], sub_out, AMD_out, SLLL_out, SLTT_out);

  assign out_2[4:2] = {3{out_2[5]}};
endmodule

module UnidadeControle (
  input  [5:0] Opcode,
  output [2:0] bitsUCselecionados,
  output Jump,
  output RegDst,
  output Regwrite,
  output AluSRC,
  output MemToReg,
  output MemRead,
  output MemWrite,
  output beqq,
  output BNEEE
);

  wire ADDI_out, ANDI_out, BEQ_out, or_5_out, or_7_out, or_9_out, ORI_out, SLTI_out;

  and R (RegDst, ~Opcode[0], ~Opcode[1], ~Opcode[2], ~Opcode[3], ~Opcode[4], ~Opcode[5]);  // AND_Gate
  and ADDI (ADDI_out, ~Opcode[0], ~Opcode[1], ~Opcode[2], Opcode[3], ~Opcode[4], ~Opcode[5]);  // AND_Gate
  and ANDI (ANDI_out, ~Opcode[0], ~Opcode[1], Opcode[2], Opcode[3], ~Opcode[4], ~Opcode[5]);  // AND_Gate
  and ORI (ORI_out, Opcode[0], ~Opcode[1], Opcode[2], Opcode[3], ~Opcode[4], ~Opcode[5]);  // AND_Gate
  and SLTI (SLTI_out, ~Opcode[0], Opcode[1], ~Opcode[2], Opcode[3], ~Opcode[4], ~Opcode[5]);  // AND_Gate
  and LW (MemRead, Opcode[0], Opcode[1], ~Opcode[2], ~Opcode[3], ~Opcode[4], Opcode[5]);  // AND_Gate
  and SW (MemWrite, Opcode[0], Opcode[1], ~Opcode[2], Opcode[3], ~Opcode[4], Opcode[5]);  // AND_Gate
  and BEQ (BEQ_out, ~Opcode[0], ~Opcode[1], Opcode[2], ~Opcode[3], ~Opcode[4], ~Opcode[5]);  // AND_Gate
  and J (Jump, ~Opcode[0], Opcode[1], ~Opcode[2], ~Opcode[3], ~Opcode[4], ~Opcode[5]);  // AND_Gate
  and bne (BNEEE, Opcode[0], ~Opcode[1], Opcode[2], ~Opcode[3], ~Opcode[4], ~Opcode[5]);  // AND_Gate
  or or_1 (Regwrite, RegDst, ADDI_out, ANDI_out, ORI_out, SLTI_out, MemRead);
  or or_2 (AluSRC, ADDI_out, ANDI_out, ORI_out, SLTI_out, MemRead, MemWrite);
  or or_3 (beqq, BEQ_out, BEQ_out);
  or or_4 (bitsUCselecionados[2], ADDI_out, ANDI_out, ORI_out, MemRead, MemWrite, or_5_out);
  or or_5 (or_5_out, BEQ_out, BNEEE);
  or or_6 (bitsUCselecionados[1], ADDI_out, SLTI_out, MemRead, MemWrite, or_7_out);
  or or_7 (or_7_out, BEQ_out, BNEEE);
  or or_8 (bitsUCselecionados[0], SLTI_out, ANDI_out, or_9_out);
  or or_9 (or_9_out, BEQ_out, BNEEE);

  assign MemToReg = MemRead;
endmodule

module ULA (
  input  [31:0] A,
  input  [31:0] B,
  input  [4:0] SHMT,
  input  [2:0] opALU,
  output Overflow,
  output [31:0] ResultadoULA,
  output Zero
);

  wire comparator_1_lt, pegar_msb_1_out_2, pegar_msb_2_out_2, pegar_msb_3_out_2;
  wire [31:0] adder_1_out, and_1_out, conversao1bit_1_out_2, or_1_out, shifter_1_out, shifter_2_out,
       subtractor_1_out, xor_1_out;

  assign xor_1_out = A ^ B;  // XOR_Gate xor_1, 32 bits wide
  Shifter #(.width(32)) shifter_1 (.in(B), .\dist (SHMT), .out(shifter_1_out));
  Shifter #(.shift("lr"), .width(32)) shifter_2 (.in(B), .\dist (SHMT), .out(shifter_2_out));
  Comparator #(.width(32)) comparator_1 (.a(A), .b(B), .lt(comparator_1_lt));  // open: gt, eq
  assign or_1_out = A | B;  // OR_Gate or_1, 32 bits wide
  assign and_1_out = A & B;  // AND_Gate and_1, 32 bits wide
  Adder #(.width(32)) adder_1 (.a(A), .b(B), .out(adder_1_out));  // open: cin, cout
  Subtractor #(.width(32)) subtractor_1 (.a(A), .b(B), .out(subtractor_1_out));  // open: bin, bout
  conversao1bit conversao1bit_1 (.in_1(comparator_1_lt), .out_2(conversao1bit_1_out_2));
  Multiplexer #(.select(3), .width(32)) multiplexer_1 (
    .in0(xor_1_out), .in1(shifter_1_out), .in2(shifter_2_out), .in3(conversao1bit_1_out_2), .in4(or_1_out),
    .in5(and_1_out), .in6(adder_1_out), .in7(subtractor_1_out), .out(ResultadoULA), .sel(opALU));
  Pegar_MSB pegar_msb_1 (.in_1(A), .out_2(pegar_msb_1_out_2));
  Pegar_MSB pegar_msb_2 (.in_1(B), .out_2(pegar_msb_2_out_2));
  Pegar_MSB pegar_msb_3 (.in_1(ResultadoULA), .out_2(pegar_msb_3_out_2));
  overflowsomasub overflowsomasub_1 (
    .opALU(opALU), .A(pegar_msb_1_out_2), .B(pegar_msb_2_out_2), .Resultado(pegar_msb_3_out_2),
    .overflow(Overflow));
  ehZero ehzero_1 (.ResultadoULA(ResultadoULA), .out_2(Zero));

  // Notes on the sheet:
  //   1 to 32
  //   000 - XOR
  //   001 - SLL
  //   010 - SRL
  //   011 - SLT
  //   100 - OR
  //   101 - AND
  //   110 - ADD
  //   111 - SUB
endmodule

module ehZero (
  input  [31:0] ResultadoULA,
  output out_2
);

  and and_1 (out_2, ~ResultadoULA[0], ~ResultadoULA[1], ~ResultadoULA[2], ~ResultadoULA[3], ~ResultadoULA[4], ~ResultadoULA[5], ~ResultadoULA[6], ~ResultadoULA[7], ~ResultadoULA[8], ~ResultadoULA[9], ~ResultadoULA[10], ~ResultadoULA[11], ~ResultadoULA[12], ~ResultadoULA[13], ~ResultadoULA[14], ~ResultadoULA[15], ~ResultadoULA[16], ~ResultadoULA[17], ~ResultadoULA[18], ~ResultadoULA[19], ~ResultadoULA[20], ~ResultadoULA[21], ~ResultadoULA[22], ~ResultadoULA[23], ~ResultadoULA[24], ~ResultadoULA[25], ~ResultadoULA[26], ~ResultadoULA[27], ~ResultadoULA[28], ~ResultadoULA[29], ~ResultadoULA[30], ~ResultadoULA[31]);  // AND_Gate
endmodule

module conversao1bit (
  input  in_1,
  output [31:0] out_2
);

  not not_1 (out_2[31], 1'b1);

  assign out_2[30:0] = {{30{out_2[31]}}, in_1};
endmodule

module Pegar_MSB (
  input  [31:0] in_1,
  output out_2
);


  assign out_2 = in_1[31];
endmodule

module overflowsomasub (
  input  [2:0] opALU,
  input  A,
  input  B,
  input  Resultado,
  output overflow
);

  wire and_1_out, and_2_out, and_3_out, and_4_out, and_5_out, and_6_out;

  and and_1 (and_1_out, opALU[2], opALU[1], ~opALU[0]);  // AND_Gate
  and and_2 (and_2_out, opALU[2], opALU[1], opALU[0]);
  and and_3 (and_3_out, and_1_out, A, B, ~Resultado);  // AND_Gate
  and and_4 (and_4_out, and_1_out, ~A, ~B, Resultado);  // AND_Gate
  and and_5 (and_5_out, and_2_out, ~A, B, Resultado);  // AND_Gate
  and and_6 (and_6_out, and_2_out, A, ~B, ~Resultado);  // AND_Gate
  or or_1 (overflow, and_3_out, and_4_out, and_5_out, and_6_out);

  // Notes on the sheet:
  //   add
  //   sub
endmodule

module extensor16para32bits (
  input  [15:0] imm16bits,
  output [31:0] imm32bits
);


  assign imm32bits = {{17{imm16bits[15]}}, imm16bits[14:0]};
endmodule

module Decodificador (
  input  [31:0] Instrucao,
  output [25:0] Addr,
  output [15:0] Imm,
  output [5:0] funct,
  output [4:0] shmt,
  output [4:0] rd,
  output [4:0] rt,
  output [4:0] rs,
  output [5:0] Opcode
);


  assign Addr = Instrucao[25:0];
  assign funct = Instrucao[5:0];
  assign Imm = Instrucao[15:0];
  assign Opcode = Instrucao[31:26];
  assign rd = Instrucao[15:11];
  assign rs = Instrucao[25:21];
  assign rt = Instrucao[20:16];
  assign shmt = Instrucao[10:6];
endmodule

module meminstr (
  input  [31:0] PcAdress,
  output [31:0] Instrucao
);

  ROM #(.addrWidth(19), .dataWidth(32)) rom_1 (.addr(PcAdress[20:2]), .data(Instrucao));
endmodule

module BancoRegistradores (
  input  [31:0] WD,
  input  clock,
  input  [4:0] LR1,
  input  [4:0] LR2,
  input  RegWrite,
  input  [4:0] WR,
  output [31:0] LD1,
  output [31:0] LD2
);

  wire demultiplexer_1_out1, demultiplexer_1_out2, demultiplexer_1_out3, demultiplexer_1_out4,
       demultiplexer_1_out5, demultiplexer_1_out6, demultiplexer_1_out7, demultiplexer_1_out8,
       demultiplexer_1_out9, demultiplexer_1_out10, demultiplexer_1_out11, demultiplexer_1_out12,
       demultiplexer_1_out13, demultiplexer_1_out14, demultiplexer_1_out15, demultiplexer_1_out16,
       demultiplexer_1_out17, demultiplexer_1_out18, demultiplexer_1_out19, demultiplexer_1_out20,
       demultiplexer_1_out21, demultiplexer_1_out22, demultiplexer_1_out23, demultiplexer_1_out24,
       demultiplexer_1_out25, demultiplexer_1_out26, demultiplexer_1_out27, demultiplexer_1_out28,
       demultiplexer_1_out29, demultiplexer_1_out30, demultiplexer_1_out31;
  wire [31:0] S0, S1, S2, S3, S4, S5, S6, S7, S8, S9, S10, S11, S12, S13, S14, S15, S16, S17, S18, S19, S20,
       S21, S22, S23, S24, S25, S26, S27, S28, S29, S30, S31;

  Demultiplexer #(.select(5)) demultiplexer_1 (
    .out1(demultiplexer_1_out1), .out2(demultiplexer_1_out2), .out3(demultiplexer_1_out3),
    .out4(demultiplexer_1_out4), .out5(demultiplexer_1_out5), .out6(demultiplexer_1_out6),
    .out7(demultiplexer_1_out7), .out8(demultiplexer_1_out8), .out9(demultiplexer_1_out9),
    .out10(demultiplexer_1_out10), .out11(demultiplexer_1_out11), .out12(demultiplexer_1_out12),
    .out13(demultiplexer_1_out13), .out14(demultiplexer_1_out14), .out15(demultiplexer_1_out15),
    .out16(demultiplexer_1_out16), .out17(demultiplexer_1_out17), .out18(demultiplexer_1_out18),
    .out19(demultiplexer_1_out19), .out20(demultiplexer_1_out20), .out21(demultiplexer_1_out21),
    .out22(demultiplexer_1_out22), .out23(demultiplexer_1_out23), .out24(demultiplexer_1_out24),
    .out25(demultiplexer_1_out25), .out26(demultiplexer_1_out26), .out27(demultiplexer_1_out27),
    .out28(demultiplexer_1_out28), .out29(demultiplexer_1_out29), .out30(demultiplexer_1_out30),
    .out31(demultiplexer_1_out31), .in(RegWrite), .sel(WR));  // open: out0
  Register #(.width(32)) register_1 (.D(WD), .en(1'b0), .clk(clock), .Q(S0));  // open: clr
  Register #(.width(32)) register_2 (.D(WD), .en(demultiplexer_1_out1), .clk(clock), .Q(S1));  // open: clr
  Register #(.width(32)) register_3 (.D(WD), .en(demultiplexer_1_out2), .clk(clock), .Q(S2));  // open: clr
  Register #(.width(32)) register_4 (.D(WD), .en(demultiplexer_1_out3), .clk(clock), .Q(S3));  // open: clr
  Register #(.width(32)) register_5 (.D(WD), .en(demultiplexer_1_out4), .clk(clock), .Q(S4));  // open: clr
  Register #(.width(32)) register_6 (.D(WD), .en(demultiplexer_1_out5), .clk(clock), .Q(S5));  // open: clr
  Register #(.width(32)) register_7 (.D(WD), .en(demultiplexer_1_out6), .clk(clock), .Q(S6));  // open: clr
  Register #(.width(32)) register_8 (.D(WD), .en(demultiplexer_1_out7), .clk(clock), .Q(S7));  // open: clr
  Register #(.width(32)) register_9 (.D(WD), .en(demultiplexer_1_out8), .clk(clock), .Q(S8));  // open: clr
  Register #(.width(32)) register_10 (.D(WD), .en(demultiplexer_1_out9), .clk(clock), .Q(S9));  // open: clr
  Register #(.width(32)) register_11 (.D(WD), .en(demultiplexer_1_out10), .clk(clock), .Q(S10));  // open: clr
  Register #(.width(32)) register_12 (.D(WD), .en(demultiplexer_1_out11), .clk(clock), .Q(S11));  // open: clr
  Register #(.width(32)) register_13 (.D(WD), .en(demultiplexer_1_out12), .clk(clock), .Q(S12));  // open: clr
  Register #(.width(32)) register_14 (.D(WD), .en(demultiplexer_1_out13), .clk(clock), .Q(S13));  // open: clr
  Register #(.width(32)) register_15 (.D(WD), .en(demultiplexer_1_out14), .clk(clock), .Q(S14));  // open: clr
  Register #(.width(32)) register_16 (.D(WD), .en(demultiplexer_1_out15), .clk(clock), .Q(S15));  // open: clr
  Register #(.width(32)) register_17 (.D(WD), .en(demultiplexer_1_out16), .clk(clock), .Q(S16));  // open: clr
  Register #(.width(32)) register_18 (.D(WD), .en(demultiplexer_1_out17), .clk(clock), .Q(S17));  // open: clr
  Register #(.width(32)) register_19 (.D(WD), .en(demultiplexer_1_out18), .clk(clock), .Q(S18));  // open: clr
  Register #(.width(32)) register_20 (.D(WD), .en(demultiplexer_1_out19), .clk(clock), .Q(S19));  // open: clr
  Register #(.width(32)) register_21 (.D(WD), .en(demultiplexer_1_out20), .clk(clock), .Q(S20));  // open: clr
  Register #(.width(32)) register_22 (.D(WD), .en(demultiplexer_1_out21), .clk(clock), .Q(S21));  // open: clr
  Register #(.width(32)) register_23 (.D(WD), .en(demultiplexer_1_out22), .clk(clock), .Q(S22));  // open: clr
  Register #(.width(32)) register_24 (.D(WD), .en(demultiplexer_1_out23), .clk(clock), .Q(S23));  // open: clr
  Register #(.width(32)) register_25 (.D(WD), .en(demultiplexer_1_out24), .clk(clock), .Q(S24));  // open: clr
  Register #(.width(32)) register_26 (.D(WD), .en(demultiplexer_1_out25), .clk(clock), .Q(S25));  // open: clr
  Register #(.width(32)) register_27 (.D(WD), .en(demultiplexer_1_out26), .clk(clock), .Q(S26));  // open: clr
  Register #(.width(32)) register_28 (.D(WD), .en(demultiplexer_1_out27), .clk(clock), .Q(S27));  // open: clr
  Register #(.width(32)) register_29 (.D(WD), .en(demultiplexer_1_out28), .clk(clock), .Q(S28));  // open: clr
  Register #(.width(32)) register_30 (.D(WD), .en(demultiplexer_1_out29), .clk(clock), .Q(S29));  // open: clr
  Register #(.width(32)) register_31 (.D(WD), .en(demultiplexer_1_out30), .clk(clock), .Q(S30));  // open: clr
  Register #(.width(32)) register_32 (.D(WD), .en(demultiplexer_1_out31), .clk(clock), .Q(S31));  // open: clr
  Multiplexer #(.select(5), .width(32)) multiplexer_1 (
    .in0(S0), .in1(S1), .in2(S2), .in3(S3), .in4(S4), .in5(S5), .in6(S6), .in7(S7), .in8(S8), .in9(S9),
    .in10(S10), .in11(S11), .in12(S12), .in13(S13), .in14(S14), .in15(S15), .in16(S16), .in17(S17),
    .in18(S18), .in19(S19), .in20(S20), .in21(S21), .in22(S22), .in23(S23), .in24(S24), .in25(S25),
    .in26(S26), .in27(S27), .in28(S28), .in29(S29), .in30(S30), .in31(S31), .out(LD1), .sel(LR1));
  Multiplexer #(.select(5), .width(32)) multiplexer_2 (
    .in0(S0), .in1(S1), .in2(S2), .in3(S3), .in4(S4), .in5(S5), .in6(S6), .in7(S7), .in8(S8), .in9(S9),
    .in10(S10), .in11(S11), .in12(S12), .in13(S13), .in14(S14), .in15(S15), .in16(S16), .in17(S17),
    .in18(S18), .in19(S19), .in20(S20), .in21(S21), .in22(S22), .in23(S23), .in24(S24), .in25(S25),
    .in26(S26), .in27(S27), .in28(S28), .in29(S29), .in30(S30), .in31(S31), .out(LD2), .sel(LR2));
endmodule

module memdados (
  input  [31:0] endereco,
  input  [31:0] escreveDado,
  input  clk,
  input  MemWrite,
  input  MemRead,
  output [31:0] dadosLidos
);

  RAM #(.addrWidth(24), .dataWidth(32), .trigger("falling")) ram_1 (
    .addr(endereco[23:0]), .we(MemWrite), .oe(MemRead), .clk(clk), .din(escreveDado), .dout(dadosLidos));
endmodule

module transformarADDR (
  input  [25:0] addr26,
  input  [31:0] PCatual,
  output [31:0] addr32
);


  assign addr32 = {PCatual[31:28], addr26, 2'b00};
endmodule
